# Fritzing sketch rpi_ws (saved by Fritzing 0.9.3b)

parts:
  Raspberry_Pi1 = Raspberry Pi B+
  LoRa_Module1 = Ra-01 - LoRa Module SX1278 [part_number=SX1278]
  U1 = TRANSCHIPTC5747 [package=camera_sfv24r-2st_2]  # not connected

nets:
  3V3: Raspberry_Pi1.3v3, LoRa_Module1.3.3V
  N1: Raspberry_Pi1.GPIO4, LoRa_Module1.DIO0
  N2: Raspberry_Pi1.GPIO22, LoRa_Module1.RESET
  N3: Raspberry_Pi1.GPIO10, LoRa_Module1.MOSI
  N4: Raspberry_Pi1.GPIO9, LoRa_Module1.MISO
  N5: Raspberry_Pi1.GPIO11, LoRa_Module1.SCK
  N6: Raspberry_Pi1.GPIO8, LoRa_Module1.NSS
  GND: Raspberry_Pi1.GND, LoRa_Module1.GND

custom parts:
  Ra-01 - LoRa Module SX1278: The Ra-01 LoRa Module featuring the SX1278 engine by Semtech. Module by AI-Thinker. Module (Ra-01) specifications from: https://www.banggood.com/Ra-01-Smart-Electronics-SX1278-LoRa-Spread-Spectrum-Wireless-Module-Ultra-Far-10KM-433M-p-1130769.html Description: Power supply: DC1.8-3.7V(3.3V) Chip: SX1278 Frequency: 433Mhz Operating temperature: -40~+85°C On Sheild Description (may vary by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
