# Fritzing sketch power_meter (saved by Fritzing 0.9.3b)

parts:
  Часть1 = Arduino Nano (Rev3.0) (ICSP)
  LoRa_Module2 = Ra-01 - LoRa Module SX1278 [part_number=SX1278]
  Часть2 = ACS712 Low Current Sensor Board v12
  Часть3 = ACS712 Low Current Sensor Board v12
  Mod1 = Voltage Sensor 25V

nets:
  N1: Часть1.D2, LoRa_Module2.DIO0
  N2: Часть1.D9, LoRa_Module2.RESET
  N3: Часть1.D10, LoRa_Module2.NSS
  N4: Часть1.D11/MOSI, LoRa_Module2.MOSI
  N5: Часть1.D12/MISO, LoRa_Module2.MISO
  GND: Часть1.GND, LoRa_Module2.GND, Часть2.GND
  5V: Часть1.5V, Часть2.5V, Часть3.5V, Mod1.+
  N6: Часть1.A3, Часть2.VO
  N7: Часть1.A1, Mod1.S
  N8: Часть1.A0, Часть3.VO
  3V3: Часть1.3V3, LoRa_Module2.3.3V
  N9: Часть1.D13/SCK, LoRa_Module2.SCK

notes:
  Current after battery
  (consumption)
  Current after controller
  (charging)
  Voltage in 12v circuit
  (after controller)

custom parts:
  Ra-01 - LoRa Module SX1278: The Ra-01 LoRa Module featuring the SX1278 engine by Semtech. Module by AI-Thinker. Module (Ra-01) specifications from: https://www.banggood.com/Ra-01-Smart-Electronics-SX1278-LoRa-Spread-Spectrum-Wireless-Module-Ultra-Far-10KM-433M-p-1130769.html Description: Power supply: DC1.8-3.7V(3.3V) Chip: SX1278 Frequency: 433Mhz Operating temperature: -40~+85°C On Sheild Description (may vary by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
