# Fritzing sketch wind_meter (saved by Fritzing 0.9.3b)

parts:
  Часть1 = Arduino Nano (Rev3.0) (ICSP)
  GY-1 = GY-271 [part_number=GY-271]
  e-radionica_com1 = LM393 LDR breakout [part_number=100027]
  LED1 = LEDs [package=led10mm]
  Часть3 = MicroSD Card Module
  LoRa_Module2 = Ra-01 - LoRa Module SX1278 [part_number=SX1278]
  Part1 = KY-012 Active Buzzer Module [package="Breakout board"]

nets:
  N1: Часть1.D2, LoRa_Module2.DIO0
  N2: Часть1.D3, Part1.S
  N3: Часть1.D5, Часть3.CS
  N4: Часть1.D8, e-radionica_com1.DO
  N5: Часть1.D9, LoRa_Module2.RESET
  N6: Часть1.D10, LoRa_Module2.NSS
  N7: Часть1.D11/MOSI, Часть3.MOSI, LoRa_Module2.MOSI
  N8: Часть1.D12/MISO, Часть3.MISO, LoRa_Module2.MISO
  GND: Часть1.GND, GY-1.GND, e-radionica_com1.GND, Часть3.GND, LoRa_Module2.GND
  VCC: Часть1.5V, Часть1.A7, GY-1.VCC, e-radionica_com1.VCC, Часть3.VCC
  N9: Часть1.A5, GY-1.SCL
  N10: Часть1.A4, GY-1.SDA
  3V3: Часть1.3V3, LED1.C, LoRa_Module2.3.3V
  N11: Часть1.D13/SCK, Часть3.SCK, LoRa_Module2.SCK

custom parts:
  GY-271: GY-271 - Electronic compass module - 3 Axis Magnetic Field Sensor HMC5883L
  Ra-01 - LoRa Module SX1278: The Ra-01 LoRa Module featuring the SX1278 engine by Semtech. Module by AI-Thinker. Module (Ra-01) specifications from: https://www.banggood.com/Ra-01-Smart-Electronics-SX1278-LoRa-Spread-Spectrum-Wireless-Module-Ultra-Far-10KM-433M-p-1130769.html Description: Power supply: DC1.8-3.7V(3.3V) Chip: SX1278 Frequency: 433Mhz Operating temperature: -40~+85°C On Sheild Description (may vary by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
  KY-012 Active Buzzer Module: Active Piezoelectric Buzzer Module Keyes KY-012, it produces single-tone sound when signal is high.
