# Fritzing sketch informer (saved by Fritzing 0.9.3b)

parts:
  Часть1 = SparkFun ESP8266 Thing
  o1 = Module display OLED I2C 128x64 SSD1306 [package=THT]
  Часть2 = Real Time Clock Module - DS1307 RTC Breakout Board

nets:
  GND: Часть1.GND, o1.GND, Часть2.GND
  VCC: Часть1.VCC, o1.VCC, Часть2.5V
  N1: Часть1.GPIO2, o1.SDA
  N2: Часть1.GPIO14, o1.SCL
  N3: Часть1.GPIO4, Часть2.SDA
  N4: Часть1.GPIO13, Часть2.SCL
  N5: Часть1.GPIO12, Часть2.SQW

custom parts:
  Module display OLED I2C 128x64 SSD1306: Ecran OLED I2C SSD163 de 128x64 avec connexion I2C
  Real Time Clock Module - DS1307 RTC Breakout Board: This a custom designed module for the DS1307 Real Time Clock. The module comes fully assembled and pre-programmed with the current time (ok, so it's our current time - MST). The included Lithium coin cell battery (CR1225 41mAh) will run the module for a minimum of 9 years (17 years typical) without external 5V power. The DS1307 is accessed via the I2C protocol. We've written a test-bed to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
