# Fritzing sketch weather_station_in (saved by Fritzing 0.9.3b)

parts:
  Часть1 = SparkFun ESP8266 Thing
  Часть2 = BME280 Breakout

nets:
  GND: Часть1.GND, Часть2.GND
  VCC: Часть1.VCC, Часть2.3.3V
  N1: Часть1.GPIO2, Часть2.SDI/SDA
  N2: Часть1.GPIO14, Часть2.SCK/SCL
