# Fritzing sketch weather_station_out (saved by Fritzing 0.9.3b)

parts:
  Часть1 = SparkFun ESP8266 Thing
  Часть2 = BME280 Breakout
  Часть3 = VEML6070 [part_number=VEML6070]  # not connected
  e-radionica_com1 = LM393 LDR breakout [part_number=100027]

nets:
  GND: Часть1.GND, Часть2.GND, e-radionica_com1.GND
  VCC: Часть1.VCC, Часть2.3.3V
  N1: Часть1.GPIO2, Часть2.SDI/SDA
  N2: Часть1.GPIO14, Часть2.SCK/SCL
  N3: Часть1.USBVCC, e-radionica_com1.VCC
  N4: Часть1.GPIO0, e-radionica_com1.DO
  N5: Часть1.ADC, e-radionica_com1.AO

custom parts:
  VEML6070: This little sensor is a great way to add UV light sensing to any microcontroller project. The VEML6070 from Vishay has a true UV A light sensor and an I2C-controlled ADC that will take readings and integrate them for you over ~60ms to 500ms.
